// Logisim project 1.2-4译码器.circ as structural Verilog: 1 circuit, main circuit main
module main (
  input  W0,
  input  W1,
  input  En,
  output Y0_W1_prime_W0_prime,
  output Y1__W1_prime_W0,
  output Y2_W1W0_prime,
  output Y3_W1W0
);

  wire not_1_out, not_2_out;

  not not_1 (not_1_out, W0);
  not not_2 (not_2_out, W1);
  and and_1 (Y0_W1_prime_W0_prime, not_1_out, not_2_out, En);
  and and_2 (Y1__W1_prime_W0, not_2_out, W0, En);
  and and_3 (Y2_W1W0_prime, not_1_out, W1, En);
  and and_4 (Y3_W1W0, W0, W1, En);

  // Notes on the sheet:
  //   242210714124 庆俊杰
endmodule
