// Logisim project 2.3-8译码器.circ as structural Verilog: 1 circuit, main circuit main
module main (
  input  W0,
  input  W1,
  input  W2,
  input  En,
  output Y0_W1_prime_W0_prime,
  output Y1_W1_prime_W0,
  output Y2_W1W0_prime,
  output Y3_W1W0,
  output Y0_W1_prime_W0_prime_2,
  output Y1_W1_prime_W0_2,
  output Y2_W1W0_prime_2,
  output Y3_W1W0_2
);

  wire and_1_out, and_2_out, not_1_out, not_2_out, not_3_out, not_4_out, not_5_out;

  not not_1 (not_1_out, W2);
  and and_1 (and_1_out, not_1_out, En);
  not not_2 (not_2_out, W0);
  not not_3 (not_3_out, W1);
  not not_4 (not_4_out, W0);
  not not_5 (not_5_out, W1);
  and and_2 (and_2_out, En, W2);
  and and_3 (Y0_W1_prime_W0_prime_2, not_4_out, not_5_out, and_2_out);
  and and_4 (Y1_W1_prime_W0_2, not_5_out, W0, and_2_out);
  and and_5 (Y2_W1W0_prime_2, not_4_out, W1, and_2_out);
  and and_6 (Y3_W1W0_2, W0, W1, and_2_out);
  and and_7 (Y0_W1_prime_W0_prime, not_2_out, not_3_out, and_1_out);
  and and_8 (Y1_W1_prime_W0, not_3_out, W0, and_1_out);
  and and_9 (Y2_W1W0_prime, not_2_out, W1, and_1_out);
  and and_10 (Y3_W1W0, W0, W1, and_1_out);

  // Notes on the sheet:
  //   242210714124 庆俊杰
endmodule
