// Logisim project 3.4-16译码器.circ as structural Verilog: 1 circuit, main circuit main
module main (
  input  \异步置1端 ,
  input  \异步清零端 ,
  input  \J_K的输入都置1 ,
  output Q0,
  output Q1,
  output Q2,
  output Q3
);

  wire CLK_out, j_k_ff_1_qn, j_k_ff_2_qn, j_k_ff_3_qn;

  Clock #(.highDuration(1), .lowDuration(1)) CLK (.out(CLK_out));
  J_K_Flip_Flop #(.trigger("rising"), .Pre_Clr_Positions("ABOVE_BELOW"), .NegatePresetClear("false"), .enable("false"), .NewFFLayout("true")) j_k_ff_1 (
    .J(\J_K的输入都置1 ), .clk(CLK_out), .K(\J_K的输入都置1 ), .Q(Q0), .Qn(j_k_ff_1_qn), .preset(\异步置1端 ),
    .reset(\异步清零端 ));
  // Digital_Oscilloscope #(.nState(10), .frontlines("rising"), .showclock("true")) digital_oscilloscope_1: pin names not known; wires that end beside it: CLK_out, Q3, Q1, Q0
  J_K_Flip_Flop #(.trigger("rising"), .Pre_Clr_Positions("ABOVE_BELOW"), .NegatePresetClear("false"), .enable("false"), .NewFFLayout("true")) j_k_ff_2 (
    .J(\J_K的输入都置1 ), .clk(j_k_ff_1_qn), .K(\J_K的输入都置1 ), .Q(Q1), .Qn(j_k_ff_2_qn), .preset(\异步置1端 ),
    .reset(\异步清零端 ));
  J_K_Flip_Flop #(.trigger("rising"), .Pre_Clr_Positions("ABOVE_BELOW"), .NegatePresetClear("false"), .enable("false"), .NewFFLayout("true")) j_k_ff_3 (
    .J(\J_K的输入都置1 ), .clk(j_k_ff_2_qn), .K(\J_K的输入都置1 ), .Q(Q2), .Qn(j_k_ff_3_qn), .preset(\异步置1端 ),
    .reset(\异步清零端 ));
  J_K_Flip_Flop #(.trigger("rising"), .Pre_Clr_Positions("ABOVE_BELOW"), .NegatePresetClear("false"), .enable("false"), .NewFFLayout("true")) j_k_ff_4 (
    .J(\J_K的输入都置1 ), .clk(j_k_ff_3_qn), .K(\J_K的输入都置1 ), .Q(Q3), .preset(\异步置1端 ), .reset(\异步清零端 ));  // open: Qn

  // Notes on the sheet:
  //   242210714124 庆俊杰
endmodule
