// Logisim project 7447显示编码器.circ as structural Verilog: 1 circuit, main circuit main
module main (
  input  \异步置1端 ,
  input  \异步清零端 ,
  input  \J_K的输入都置1 ,
  input  in_4,
  input  in_5,
  input  in_6
);

  wire CLK_out, digital_oscilloscope_1_p2, digital_oscilloscope_1_p3, j_k_ff_1_q, j_k_ff_1_qn, j_k_ff_2_qn,
       j_k_ff_3_qn, n7447_1_pin2, n7447_1_pin9, n7447_1_pin10, n7447_1_pin11, n7447_1_pin12, n7447_1_pin13,
       n7447_1_pin14, n7447_1_pin15;

  Clock #(.highDuration(1), .lowDuration(1)) CLK (.out(CLK_out));
  J_K_Flip_Flop #(.trigger("rising"), .Pre_Clr_Positions("ABOVE_BELOW"), .NegatePresetClear("false"), .enable("false"), .NewFFLayout("true")) j_k_ff_1 (
    .J(\J_K的输入都置1 ), .clk(CLK_out), .K(\J_K的输入都置1 ), .Q(j_k_ff_1_q), .Qn(j_k_ff_1_qn), .preset(\异步置1端 ),
    .reset(\异步清零端 ));
  // Digital_Oscilloscope #(.nState(10), .frontlines("rising"), .showclock("true")) digital_oscilloscope_1: pin names not known; wires that end beside it: CLK_out, digital_oscilloscope_1_p2, digital_oscilloscope_1_p3, j_k_ff_1_q, 1'b1, 1'b0
  _7447 #(.VccGndPorts("false"), .ShowInternalStructure("false")) u_7447_1 (
    .pin1(digital_oscilloscope_1_p3), .pin2(n7447_1_pin2), .pin3(in_4), .pin4(in_5), .pin5(in_6),
    .pin6(digital_oscilloscope_1_p2), .pin7(j_k_ff_1_q), .pin15(n7447_1_pin15), .pin14(n7447_1_pin14),
    .pin13(n7447_1_pin13), .pin12(n7447_1_pin12), .pin11(n7447_1_pin11), .pin10(n7447_1_pin10),
    .pin9(n7447_1_pin9));
  J_K_Flip_Flop #(.trigger("rising"), .Pre_Clr_Positions("ABOVE_BELOW"), .NegatePresetClear("false"), .enable("false"), .NewFFLayout("true")) j_k_ff_2 (
    .J(\J_K的输入都置1 ), .clk(j_k_ff_1_qn), .K(\J_K的输入都置1 ), .Q(digital_oscilloscope_1_p3), .Qn(j_k_ff_2_qn),
    .preset(\异步置1端 ), .reset(\异步清零端 ));
  J_K_Flip_Flop #(.trigger("rising"), .Pre_Clr_Positions("ABOVE_BELOW"), .NegatePresetClear("false"), .enable("false"), .NewFFLayout("true")) j_k_ff_3 (
    .J(\J_K的输入都置1 ), .clk(j_k_ff_2_qn), .K(\J_K的输入都置1 ), .Q(n7447_1_pin2), .Qn(j_k_ff_3_qn),
    .preset(\异步置1端 ), .reset(\异步清零端 ));
  J_K_Flip_Flop #(.trigger("rising"), .Pre_Clr_Positions("ABOVE_BELOW"), .NegatePresetClear("false"), .enable("false"), .NewFFLayout("true")) j_k_ff_4 (
    .J(\J_K的输入都置1 ), .clk(j_k_ff_3_qn), .K(\J_K的输入都置1 ), .Q(digital_oscilloscope_1_p2), .preset(\异步置1端 ),
    .reset(\异步清零端 ));  // open: Qn
  _7_Segment_Display #(.active("true")) u_7_segment_display_1 (
    .g(n7447_1_pin14), .f(n7447_1_pin15), .a(n7447_1_pin13), .b(n7447_1_pin12), .e(n7447_1_pin9),
    .d(n7447_1_pin10), .c(n7447_1_pin11));  // open: dp

  // Notes on the sheet:
  //   242210714124 庆俊杰
endmodule
