// Logisim project Q1.circ as structural Verilog: 1 circuit, main circuit main
module main (
  input  A,
  input  B,
  input  C,
  input  D,
  output E
);

  wire and_1_out, and_2_out, and_3_out, and_4_out, not_1_out, not_2_out, or_1_out, or_3_out;

  not not_1 (not_1_out, B);
  not not_2 (not_2_out, A);
  and and_1 (and_1_out, not_2_out, not_1_out);
  and and_2 (and_2_out, not_1_out, C);
  and and_3 (and_3_out, C, D);
  and and_4 (and_4_out, D, not_2_out);
  or or_1 (or_1_out, and_1_out, and_2_out);
  or or_2 (E, or_1_out, or_3_out);
  or or_3 (or_3_out, and_3_out, and_4_out);

  // Notes on the sheet:
  //   庆俊杰 人工智能 242210714124
endmodule
