// Logisim project Q2.circ as structural Verilog: 1 circuit, main circuit main
module main (
  input  A,
  input  B,
  input  C,
  input  D,
  output Y
);

  wire and_1_out, and_2_out, and_3_out, and_4_out;

  and and_1 (and_1_out, A, B, C);
  and and_2 (and_2_out, D, B, A);
  and and_3 (and_3_out, B, C, D);
  and and_4 (and_4_out, A, D, C);
  or or_1 (Y, and_1_out, and_2_out, and_3_out, and_4_out);

  // Notes on the sheet:
  //   242210714124 庆俊杰 人工智能
endmodule
