// Logisim project Q3.circ as structural Verilog: 1 circuit, main circuit main
module main (
  input  A,
  input  B,
  input  C,
  output X,
  output Y
);

  wire and_1_out, and_2_out, and_3_out, xor_1_out;

  xor xor_1 (xor_1_out, A, B);
  and and_1 (and_1_out, A, B);
  and and_2 (and_2_out, C, B);
  and and_3 (and_3_out, C, A);
  xor xor_2 (X, xor_1_out, C);
  nor nor_1 (Y, and_1_out, and_2_out, and_3_out);

  // Notes on the sheet:
  //   242210714124 庆俊杰 人工智能
endmodule
