// Logisim project S1.circ as structural Verilog: 1 circuit, main circuit main
module main (
  input  SD,
  input  RD,
  output Q,
  output Q_prime
);

  nand nand_1 (Q, SD, Q_prime);
  nand nand_2 (Q_prime, Q, RD);

  // Notes on the sheet:
  //   242210714124 庆俊杰 人工智能
endmodule
