// Logisim project S4.circ as structural Verilog: 1 circuit, main circuit main
module main (
  output Q,
  output Q1
);

  wire clock_1_out, undriven;

  Clock #(.highDuration(1), .lowDuration(1)) clock_1 (.out(clock_1_out));
  T_Flip_Flop #(.trigger("rising"), .Pre_Clr_Positions("ABOVE_BELOW"), .NegatePresetClear("false"), .enable("false"), .NewFFLayout("true")) t_ff_1 (
    .clk(clock_1_out), .Q(Q), .Qn(Q1), .preset(undriven));  // open: T, reset
endmodule
