// Logisim project 六进制计数器.circ as structural Verilog: 1 circuit, main circuit main
module main (
  input  in_1,
  output Q0,
  output Q1,
  output Q2,
  output \进位输出 
);

  wire and_1_out, and_2_out, and_3_out, clock_1_out, j_k_ff_2_qn, j_k_ff_3_qn;

  Clock #(.highDuration(1), .lowDuration(1)) clock_1 (.out(clock_1_out));
  J_K_Flip_Flop #(.trigger("rising"), .Pre_Clr_Positions("ABOVE_BELOW"), .NegatePresetClear("false"), .enable("false"), .NewFFLayout("true")) j_k_ff_1 (
    .J(in_1), .clk(clock_1_out), .K(clock_1_out), .Q(Q0));  // open: Qn, preset, reset
  // Digital_Oscilloscope #(.nState(10), .frontlines("rising"), .showclock("true")) digital_oscilloscope_1: pin names not known; wires that end beside it: clock_1_out, Q0, Q1, Q2, \进位输出 
  and and_1 (and_1_out, j_k_ff_3_qn, Q0);
  J_K_Flip_Flop #(.trigger("rising"), .Pre_Clr_Positions("ABOVE_BELOW"), .NegatePresetClear("false"), .enable("false"), .NewFFLayout("true")) j_k_ff_2 (
    .J(and_1_out), .clk(clock_1_out), .K(Q0), .Q(Q1), .Qn(j_k_ff_2_qn));  // open: preset, reset
  and and_2 (and_2_out, Q0, Q1);
  and and_3 (and_3_out, j_k_ff_2_qn, Q0);
  J_K_Flip_Flop #(.trigger("rising"), .Pre_Clr_Positions("ABOVE_BELOW"), .NegatePresetClear("false"), .enable("false"), .NewFFLayout("true")) j_k_ff_3 (
    .J(and_2_out), .clk(clock_1_out), .K(and_3_out), .Q(Q2), .Qn(j_k_ff_3_qn));  // open: preset, reset
  and and_4 (\进位输出 , Q0, Q2);

  // Notes on the sheet:
  //   242210714124 庆俊杰
endmodule
