// Logisim project 左移.circ as structural Verilog: 1 circuit, main circuit main
module main (
  input  strat,
  output out_2,
  output out_3,
  output out_4,
  output out_5
);

  wire digital_oscilloscope_1_p1, not_1_out;

  D_Flip_Flop #(.trigger("rising"), .Pre_Clr_Positions("ABOVE_BELOW"), .NegatePresetClear("false"), .enable("false"), .NewFFLayout("true")) d_ff_1 (
    .clk(digital_oscilloscope_1_p1), .D(out_3), .Q(out_2), .reset(not_1_out));  // open: Qn, preset
  // Digital_Oscilloscope #(.nState(10), .frontlines("rising"), .showclock("true")) digital_oscilloscope_1: pin names not known; wires that end beside it: digital_oscilloscope_1_p1, out_2, out_3, out_4, out_5
  D_Flip_Flop #(.trigger("rising"), .Pre_Clr_Positions("ABOVE_BELOW"), .NegatePresetClear("false"), .enable("false"), .NewFFLayout("true")) d_ff_2 (
    .clk(digital_oscilloscope_1_p1), .D(out_4), .Q(out_3), .reset(not_1_out));  // open: Qn, preset
  D_Flip_Flop #(.trigger("rising"), .Pre_Clr_Positions("ABOVE_BELOW"), .NegatePresetClear("false"), .enable("false"), .NewFFLayout("true")) d_ff_3 (
    .clk(digital_oscilloscope_1_p1), .D(out_5), .Q(out_4), .reset(not_1_out));  // open: Qn, preset
  D_Flip_Flop #(.trigger("rising"), .Pre_Clr_Positions("ABOVE_BELOW"), .NegatePresetClear("false"), .enable("false"), .NewFFLayout("true")) d_ff_4 (
    .clk(digital_oscilloscope_1_p1), .D(out_4), .Q(out_5), .preset(not_1_out));  // open: Qn, reset
  not not_1 (not_1_out, strat);
  Clock #(.highDuration(1), .lowDuration(1)) clock_1 (.out(digital_oscilloscope_1_p1));

  // Notes on the sheet:
  //   242210714124 庆俊杰
endmodule
