// Logisim project 并行存取.circ as structural Verilog: 1 circuit, main circuit main
module main (
  input  \异步置1 ,
  input  \串行输入 ,
  input  Load,
  input  \异步清0 ,
  input  D3,
  input  D2,
  input  D3_2,
  input  D3_3,
  output out_9,
  output out_10,
  output out_11,
  output out_12,
  output out_13
);

  wire clock_1_out, multiplexer_1_out, multiplexer_2_out, multiplexer_3_out, multiplexer_4_out;

  Clock #(.highDuration(1), .lowDuration(1)) clock_1 (.out(clock_1_out));
  Multiplexer #(.select(1), .width(1), .disabled("Z"), .enable("false")) multiplexer_1 (
    .in0(\串行输入 ), .in1(D3), .out(multiplexer_1_out), .sel(Load));
  D_Flip_Flop #(.trigger("rising"), .Pre_Clr_Positions("ABOVE_BELOW"), .NegatePresetClear("false"), .enable("false"), .NewFFLayout("true")) d_ff_1 (
    .clk(clock_1_out), .D(multiplexer_1_out), .Q(out_9), .preset(\异步置1 ), .reset(\异步清0 ));  // open: Qn
  Multiplexer #(.select(1), .width(1), .disabled("Z"), .enable("false")) multiplexer_2 (
    .in0(out_9), .in1(D2), .out(multiplexer_2_out), .sel(Load));
  D_Flip_Flop #(.trigger("rising"), .Pre_Clr_Positions("ABOVE_BELOW"), .NegatePresetClear("false"), .enable("false"), .NewFFLayout("true")) d_ff_2 (
    .clk(clock_1_out), .D(multiplexer_2_out), .Q(out_10), .preset(\异步置1 ), .reset(\异步清0 ));  // open: Qn
  Multiplexer #(.select(1), .width(1), .disabled("Z"), .enable("false")) multiplexer_3 (
    .in0(out_10), .in1(D3_2), .out(multiplexer_3_out), .sel(Load));
  D_Flip_Flop #(.trigger("rising"), .Pre_Clr_Positions("ABOVE_BELOW"), .NegatePresetClear("false"), .enable("false"), .NewFFLayout("true")) d_ff_3 (
    .clk(clock_1_out), .D(multiplexer_3_out), .Q(out_11), .preset(\异步置1 ), .reset(\异步清0 ));  // open: Qn
  Multiplexer #(.select(1), .width(1), .disabled("Z"), .enable("false")) multiplexer_4 (
    .in0(out_11), .in1(D3_3), .out(multiplexer_4_out), .sel(Load));
  D_Flip_Flop #(.trigger("rising"), .Pre_Clr_Positions("ABOVE_BELOW"), .NegatePresetClear("false"), .enable("false"), .NewFFLayout("true")) d_ff_4 (
    .clk(clock_1_out), .D(multiplexer_4_out), .Q(out_12), .preset(\异步置1 ), .reset(\异步清0 ));  // open: Qn

  assign out_13 = out_12;

  // Notes on the sheet:
  //   242210714124 庆俊杰
endmodule
